// Digital circuit 4_Bit_Adder_with_Flags.dig as structural Verilog
module _4_Bit_Adder_with_Flags (
  input  A3,
  input  A2,
  input  A1,
  input  A0,
  input  B3,
  input  B2,
  input  B1,
  input  B0,
  input  SU,
  input  EO,
  input  CLK,
  output Q3,
  output Q2,
  output Q1,
  output Q0,
  output CAR,
  output NEG,
  output Z
);

  wire and_1_out, and_2_out, and_3_out, and_4_out, and_5_out, and_6_out, and_7_out, and_8_out, and_9_out,
       and_10_out, and_11_out, not_1_out, not_2_out, not_3_out, not_4_out, or_2_out, or_3_out, or_4_out,
       xor_1_out, xor_2_out, xor_3_out, xor_4_out, xor_5_out, xor_6_out, xor_7_out, xor_8_out, xor_10_out,
       xor_11_out, xor_12_out;

  and and_1 (and_1_out, CLK, EO);
  xor xor_1 (xor_1_out, B3, SU);
  xor xor_2 (xor_2_out, B2, SU);
  xor xor_3 (xor_3_out, B1, SU);
  xor xor_4 (xor_4_out, B0, SU);
  xor xor_5 (xor_5_out, A3, xor_1_out);
  and and_2 (and_2_out, A3, xor_1_out);
  xor xor_6 (xor_6_out, A2, xor_2_out);
  and and_3 (and_3_out, A2, xor_2_out);
  xor xor_7 (xor_7_out, A1, xor_3_out);
  and and_4 (and_4_out, A1, xor_3_out);
  xor xor_8 (xor_8_out, A0, xor_4_out);
  and and_5 (and_5_out, A0, xor_4_out);
  xor xor_9 (NEG, or_2_out, xor_5_out);
  and and_6 (and_6_out, xor_5_out, or_2_out);
  xor xor_10 (xor_10_out, or_3_out, xor_6_out);
  and and_7 (and_7_out, xor_6_out, or_3_out);
  xor xor_11 (xor_11_out, or_4_out, xor_7_out);
  and and_8 (and_8_out, xor_7_out, or_4_out);
  xor xor_12 (xor_12_out, SU, xor_8_out);
  and and_9 (and_9_out, xor_8_out, SU);
  or or_1 (CAR, and_6_out, and_2_out);
  or or_2 (or_2_out, and_7_out, and_3_out);
  or or_3 (or_3_out, and_8_out, and_4_out);
  or or_4 (or_4_out, and_9_out, and_5_out);
  and and_10 (and_10_out, not_1_out, not_2_out);
  not not_1 (not_1_out, NEG);
  not not_2 (not_2_out, xor_10_out);
  not not_3 (not_3_out, xor_11_out);
  not not_4 (not_4_out, xor_12_out);
  Tri_State_Buffer tri_state_buffer_1 (.IN(NEG), .EN(and_1_out), .OUT(Q3));
  Tri_State_Buffer tri_state_buffer_2 (.IN(xor_10_out), .EN(and_1_out), .OUT(Q2));
  Tri_State_Buffer tri_state_buffer_3 (.IN(xor_11_out), .EN(and_1_out), .OUT(Q1));
  Tri_State_Buffer tri_state_buffer_4 (.IN(xor_12_out), .EN(and_1_out), .OUT(Q0));
  and and_11 (and_11_out, and_10_out, not_3_out);
  and and_12 (Z, and_11_out, not_4_out);

  // Notes on the sheet:
  //   Carry In
endmodule
