// Digital circuit 4_Bit_Reg_v2.dig as structural Verilog
module _4_Bit_Reg_v2 (
  input  LD,
  input  D0,
  input  D1,
  input  D2,
  input  D3,
  input  CLK,
  input  EO,
  output O0,
  output O1,
  output O2,
  output O3
);

  wire and_1_out, and_2_out, and_3_out, and_4_out, and_5_out, and_6_out, and_7_out, and_8_out, and_9_out,
       and_10_out, and_11_out, and_12_out, and_13_out, and_14_out, and_15_out, and_16_out, and_17_out,
       nor_1_out, nor_2_out, nor_3_out, nor_4_out, nor_5_out, nor_6_out, nor_7_out, nor_8_out, not_1_out,
       not_2_out, not_3_out, not_4_out, not_5_out, not_6_out, not_7_out, not_8_out, or_1_out, or_2_out,
       or_3_out, or_4_out;

  and and_1 (and_1_out, EO, CLK);
  not not_1 (not_1_out, LD);
  not not_2 (not_2_out, LD);
  not not_3 (not_3_out, LD);
  not not_4 (not_4_out, LD);
  and and_2 (and_2_out, nor_1_out, not_1_out);
  and and_3 (and_3_out, LD, D0);
  and and_4 (and_4_out, nor_3_out, not_2_out);
  and and_5 (and_5_out, LD, D1);
  and and_6 (and_6_out, nor_5_out, not_3_out);
  and and_7 (and_7_out, LD, D2);
  and and_8 (and_8_out, nor_7_out, not_4_out);
  and and_9 (and_9_out, LD, D3);
  or or_1 (or_1_out, and_2_out, and_3_out);
  or or_2 (or_2_out, and_4_out, and_5_out);
  or or_3 (or_3_out, and_6_out, and_7_out);
  or or_4 (or_4_out, and_8_out, and_9_out);
  not not_5 (not_5_out, or_1_out);
  not not_6 (not_6_out, or_2_out);
  not not_7 (not_7_out, or_3_out);
  not not_8 (not_8_out, or_4_out);
  and and_10 (and_10_out, not_5_out, CLK);
  and and_11 (and_11_out, CLK, or_1_out);
  and and_12 (and_12_out, not_6_out, CLK);
  and and_13 (and_13_out, CLK, or_2_out);
  and and_14 (and_14_out, not_7_out, CLK);
  and and_15 (and_15_out, CLK, or_3_out);
  and and_16 (and_16_out, not_8_out, CLK);
  and and_17 (and_17_out, CLK, or_4_out);
  nor nor_1 (nor_1_out, and_10_out, nor_2_out);
  nor nor_2 (nor_2_out, nor_1_out, and_11_out);
  nor nor_3 (nor_3_out, and_12_out, nor_4_out);
  nor nor_4 (nor_4_out, nor_3_out, and_13_out);
  nor nor_5 (nor_5_out, and_14_out, nor_6_out);
  nor nor_6 (nor_6_out, nor_5_out, and_15_out);
  nor nor_7 (nor_7_out, and_16_out, nor_8_out);
  nor nor_8 (nor_8_out, nor_7_out, and_17_out);
  Tri_State_Buffer tri_state_buffer_1 (.IN(nor_1_out), .EN(and_1_out), .OUT(O0));
  Tri_State_Buffer tri_state_buffer_2 (.IN(nor_5_out), .EN(and_1_out), .OUT(O2));
  Tri_State_Buffer tri_state_buffer_3 (.IN(nor_3_out), .EN(and_1_out), .OUT(O1));
  Tri_State_Buffer tri_state_buffer_4 (.IN(nor_7_out), .EN(and_1_out), .OUT(O3));
endmodule
