// Digital circuit ALU_with_Flags_IC_Simpler.dig as structural Verilog
module ALU_with_Flags_IC_Simpler (
  input  A1,
  input  B1,
  input  SU,
  input  EO,
  input  CLK,
  input  B2,
  input  B3,
  input  B4,
  input  A2,
  input  A3,
  input  A4,
  output Z,
  output CAR,
  output NEG,
  output _1,
  output _2,
  output _3,
  output _4
);

  wire _3_STATE_pin1, _74283_1_pin1, _74283_1_pin4, _74283_1_pin13, AND_pin3, AND_pin6, NOT_pin2, NOT_pin4,
       NOT_pin6, NOT_pin8, XOR_pin3, XOR_pin6, XOR_pin8, XOR_pin11;

  _7486 XOR (
    .pin1(SU), .pin2(B1), .pin3(XOR_pin3), .pin4(SU), .pin5(B2), .pin6(XOR_pin6), .pin7(1'b0),
    .pin8(XOR_pin8), .pin9(SU), .pin10(B3), .pin11(XOR_pin11), .pin12(SU), .pin13(B4), .pin14(1'b1));
  _74283 _74283_1 (
    .pin1(_74283_1_pin1), .pin2(XOR_pin6), .pin3(A2), .pin4(_74283_1_pin4), .pin5(A1), .pin6(XOR_pin3),
    .pin7(SU), .pin8(1'b0), .pin9(CAR), .pin10(NEG), .pin11(XOR_pin11), .pin12(A4), .pin13(_74283_1_pin13),
    .pin14(A3), .pin15(XOR_pin8), .pin16(1'b1));
  _74126 _3_STATE (
    .pin1(_3_STATE_pin1), .pin2(_74283_1_pin4), .pin3(_1), .pin4(_3_STATE_pin1), .pin5(_74283_1_pin1),
    .pin6(_2), .pin7(1'b0), .pin8(_3), .pin9(_74283_1_pin13), .pin10(_3_STATE_pin1), .pin11(_4), .pin12(NEG),
    .pin13(_3_STATE_pin1), .pin14(1'b1));
  _7404 NOT (
    .pin1(_74283_1_pin4), .pin2(NOT_pin2), .pin3(_74283_1_pin1), .pin4(NOT_pin4), .pin5(_74283_1_pin13),
    .pin6(NOT_pin6), .pin7(1'b0), .pin8(NOT_pin8), .pin9(NEG), .pin11(1'b1), .pin13(1'b1), .pin14(1'b1));  // open: pin10, pin12
  _7408 AND (
    .pin1(NOT_pin2), .pin2(NOT_pin4), .pin3(AND_pin3), .pin4(AND_pin3), .pin5(NOT_pin6), .pin6(AND_pin6),
    .pin7(1'b0), .pin8(Z), .pin9(AND_pin6), .pin10(NOT_pin8), .pin11(_3_STATE_pin1), .pin12(CLK), .pin13(EO),
    .pin14(1'b1));
endmodule
