// Digital circuit Binary_Counter_with_Load.dig as structural Verilog
module Binary_Counter_with_Load (
  input  CLR,
  input  LD,
  input  INC,
  input  CLK,
  input  D0_2,
  input  D1_2,
  input  D2_2,
  input  D3_2,
  input  OUT,
  output D0,
  output D1,
  output D2,
  output D3
);

  wire and_1_out, and_2_out, and_3_out, and_4_out, and_5_out, and_6_out, and_7_out, and_8_out, and_9_out,
       and_10_out, and_11_out, and_12_out, and_13_out, and_14_out, jk_ff_1_q, jk_ff_2_q, jk_ff_3_q,
       jk_ff_4_q, not_1_out, not_2_out, not_3_out, not_4_out, not_5_out, not_6_out, or_1_out, or_2_out,
       or_3_out, or_4_out, or_5_out, or_6_out, or_7_out, or_8_out;

  not not_1 (not_1_out, D0_2);
  not not_2 (not_2_out, D1_2);
  not not_3 (not_3_out, D2_2);
  not not_4 (not_4_out, D3_2);
  not not_5 (not_5_out, CLR);
  not not_6 (not_6_out, LD);
  and and_1 (and_1_out, not_5_out, LD);
  and and_2 (and_2_out, not_5_out, not_6_out, INC);
  and and_3 (and_3_out, and_1_out, D0_2);
  and and_4 (and_4_out, and_1_out, not_1_out);
  and and_5 (and_5_out, and_1_out, D1_2);
  and and_6 (and_6_out, and_1_out, not_2_out);
  and and_7 (and_7_out, and_1_out, D2_2);
  and and_8 (and_8_out, and_1_out, not_3_out);
  and and_9 (and_9_out, and_1_out, D3_2);
  and and_10 (and_10_out, and_1_out, not_4_out);
  and and_11 (and_11_out, jk_ff_1_q, and_2_out);
  and and_12 (and_12_out, jk_ff_2_q, and_11_out);
  and and_13 (and_13_out, jk_ff_3_q, and_12_out);
  and and_14 (and_14_out, CLR, OUT);
  or or_1 (or_1_out, and_2_out, and_3_out);
  or or_2 (or_2_out, and_2_out, CLR, and_4_out);
  or or_3 (or_3_out, and_11_out, and_5_out);
  or or_4 (or_4_out, and_11_out, CLR, and_6_out);
  or or_5 (or_5_out, and_12_out, and_7_out);
  or or_6 (or_6_out, and_12_out, CLR, and_8_out);
  or or_7 (or_7_out, and_13_out, and_9_out);
  or or_8 (or_8_out, and_13_out, CLR, and_10_out);
  JK_FF jk_ff_1 (.J(or_1_out), .C(CLK), .K(or_2_out), .Q(jk_ff_1_q));  // open: nQ
  JK_FF jk_ff_2 (.J(or_3_out), .C(CLK), .K(or_4_out), .Q(jk_ff_2_q));  // open: nQ
  JK_FF jk_ff_3 (.J(or_5_out), .C(CLK), .K(or_6_out), .Q(jk_ff_3_q));  // open: nQ
  JK_FF jk_ff_4 (.J(or_7_out), .C(CLK), .K(or_8_out), .Q(jk_ff_4_q));  // open: nQ
  Tri_State_Buffer tri_state_buffer_1 (.IN(jk_ff_1_q), .EN(and_14_out), .OUT(D0));
  Tri_State_Buffer tri_state_buffer_2 (.IN(jk_ff_2_q), .EN(and_14_out), .OUT(D1));
  Tri_State_Buffer tri_state_buffer_3 (.IN(jk_ff_3_q), .EN(and_14_out), .OUT(D2));
  Tri_State_Buffer tri_state_buffer_4 (.IN(jk_ff_4_q), .EN(and_14_out), .OUT(D3));
endmodule
