// Digital circuit D_Latch.dig as structural Verilog
module D_Latch (
  input  IN,
  input  EN,
  output Q,
  output Q_2
);

  wire and_1_out, and_2_out, not_1_out;

  not not_1 (not_1_out, IN);
  and and_1 (and_1_out, not_1_out, EN);
  and and_2 (and_2_out, EN, IN);
  nor nor_1 (Q, and_1_out, Q_2);
  nor nor_2 (Q_2, Q, and_2_out);
endmodule
