// Digital circuit Full_Assembly.dig as structural Verilog
module Full_Assembly (
  input  OUT,
  input  SEL,
  input  SEL_2,
  input  in_4
);

  wire _74189_1_pin2, _74189_1_pin5, _74189_1_pin7, _74189_1_pin9, _74189_1_pin11, and_1_out, and_2_out,
       and_3_out, and_4_out, and_5_out, and_6_out, and_7_out, and_8_out, and_9_out, and_10_out, and_11_out,
       and_12_out, and_13_out, and_14_out, and_15_out, and_16_out, and_17_out, and_18_out, and_19_out,
       and_20_out, and_21_out, and_22_out, and_23_out, and_24_out, and_25_out, and_26_out, and_27_out,
       and_28_out, and_29_out, and_30_out, and_31_out, and_32_out, and_33_out, d_latch_1_q, d_latch_2_q,
       d_latch_3_q, d_latch_4_q, d_latch_5_q, d_latch_6_q, d_latch_7_q, d_latch_8_q, dipswitch_1_out,
       dipswitch_2_out, dipswitch_3_out, dipswitch_4_out, dipswitch_5_out, dipswitch_6_out, dipswitch_7_out,
       dipswitch_8_out, LD_Reg_2_out, LD_Reg_out, not_1_out, not_2_out, not_3_out, not_4_out, not_5_out,
       not_6_out, not_7_out, not_8_out, not_9_out, not_10_out, not_11_out, not_13_out, not_14_out,
       not_15_out, not_16_out, or_1_out, or_2_out, or_3_out, or_4_out, or_5_out, or_6_out, or_7_out,
       or_8_out, or_9_out, or_10_out, or_11_out, or_12_out, or_13_out, or_14_out, or_15_out, or_16_out,
       tri_state_buffer_1_out, tri_state_buffer_2_out, tri_state_buffer_3_out, tri_state_buffer_4_out, W_out;

  Button W (.out(W_out));
  not not_1 (not_1_out, W_out);
  Button LD_Reg (.out(LD_Reg_out));
  not not_2 (not_2_out, SEL_2);
  LED led_1 (.in(not_2_out));
  and and_1 (and_1_out, OUT, in_4);
  LED led_2 (.in(not_3_out));
  not not_3 (not_3_out, SEL);
  Button LD_Reg_2 (.out(LD_Reg_2_out));
  not not_4 (not_4_out, LD_Reg_out);
  not not_5 (not_5_out, LD_Reg_out);
  not not_6 (not_6_out, LD_Reg_out);
  not not_7 (not_7_out, LD_Reg_out);
  and and_2 (and_2_out, d_latch_1_q, not_4_out);
  and and_3 (and_3_out, LD_Reg_out, tri_state_buffer_1_out);
  and and_4 (and_4_out, d_latch_2_q, not_5_out);
  and and_5 (and_5_out, LD_Reg_out, tri_state_buffer_3_out);
  and and_6 (and_6_out, d_latch_3_q, not_6_out);
  and and_7 (and_7_out, LD_Reg_out, tri_state_buffer_2_out);
  and and_8 (and_8_out, d_latch_4_q, not_7_out);
  and and_9 (and_9_out, LD_Reg_out, tri_state_buffer_4_out);
  not not_8 (not_8_out, LD_Reg_2_out);
  not not_9 (not_9_out, LD_Reg_2_out);
  not not_10 (not_10_out, LD_Reg_2_out);
  not not_11 (not_11_out, LD_Reg_2_out);
  or or_1 (or_1_out, and_2_out, and_3_out);
  or or_2 (or_2_out, and_4_out, and_5_out);
  or or_3 (or_3_out, and_6_out, and_7_out);
  or or_4 (or_4_out, and_8_out, and_9_out);
  and and_10 (and_10_out, d_latch_5_q, not_8_out);
  and and_11 (and_11_out, LD_Reg_2_out, tri_state_buffer_1_out);
  and and_12 (and_12_out, d_latch_6_q, not_9_out);
  and and_13 (and_13_out, LD_Reg_2_out, tri_state_buffer_3_out);
  and and_14 (and_14_out, d_latch_7_q, not_10_out);
  and and_15 (and_15_out, LD_Reg_2_out, tri_state_buffer_2_out);
  and and_16 (and_16_out, d_latch_8_q, not_11_out);
  and and_17 (and_17_out, LD_Reg_2_out, tri_state_buffer_4_out);
  D_Latch d_latch_1 (.IN(or_1_out), .EN(in_4), .Q(d_latch_1_q));  // open: Q_2
  D_Latch d_latch_2 (.IN(or_2_out), .EN(in_4), .Q(d_latch_2_q));  // open: Q_2
  D_Latch d_latch_3 (.IN(or_3_out), .EN(in_4), .Q(d_latch_3_q));  // open: Q_2
  D_Latch d_latch_4 (.IN(or_4_out), .EN(in_4), .Q(d_latch_4_q));  // open: Q_2
  or or_5 (or_5_out, and_10_out, and_11_out);
  or or_6 (or_6_out, and_12_out, and_13_out);
  or or_7 (or_7_out, and_14_out, and_15_out);
  or or_8 (or_8_out, and_16_out, and_17_out);
  DipSwitch dipswitch_1 (.out(dipswitch_1_out));
  LED led_3 (.in(SEL_2));
  D_Latch d_latch_5 (.IN(or_5_out), .EN(in_4), .Q(d_latch_5_q));  // open: Q_2
  D_Latch d_latch_6 (.IN(or_6_out), .EN(in_4), .Q(d_latch_6_q));  // open: Q_2
  D_Latch d_latch_7 (.IN(or_7_out), .EN(in_4), .Q(d_latch_7_q));  // open: Q_2
  D_Latch d_latch_8 (.IN(or_8_out), .EN(in_4), .Q(d_latch_8_q));  // open: Q_2
  DipSwitch dipswitch_2 (.out(dipswitch_2_out));
  DipSwitch dipswitch_3 (.out(dipswitch_3_out));
  and and_18 (and_18_out, d_latch_1_q, not_2_out);
  and and_19 (and_19_out, dipswitch_1_out, SEL_2);
  and and_20 (and_20_out, d_latch_2_q, not_2_out);
  and and_21 (and_21_out, dipswitch_3_out, SEL_2);
  and and_22 (and_22_out, d_latch_3_q, not_2_out);
  and and_23 (and_23_out, dipswitch_2_out, SEL_2);
  and and_24 (and_24_out, d_latch_4_q, not_2_out);
  and and_25 (and_25_out, dipswitch_4_out, SEL_2);
  DipSwitch dipswitch_4 (.out(dipswitch_4_out));
  DipSwitch dipswitch_5 (.out(dipswitch_5_out));
  LED led_4 (.in(SEL));
  DipSwitch dipswitch_6 (.out(dipswitch_6_out));
  DipSwitch dipswitch_7 (.out(dipswitch_7_out));
  or or_9 (or_9_out, and_18_out, and_19_out);
  or or_10 (or_10_out, and_20_out, and_21_out);
  or or_11 (or_11_out, and_22_out, and_23_out);
  or or_12 (or_12_out, and_24_out, and_25_out);
  and and_26 (and_26_out, not_3_out, d_latch_5_q);
  and and_27 (and_27_out, SEL, dipswitch_5_out);
  and and_28 (and_28_out, not_3_out, d_latch_6_q);
  and and_29 (and_29_out, SEL, dipswitch_6_out);
  and and_30 (and_30_out, not_3_out, d_latch_7_q);
  and and_31 (and_31_out, SEL, dipswitch_7_out);
  and and_32 (and_32_out, not_3_out, d_latch_8_q);
  and and_33 (and_33_out, SEL, dipswitch_8_out);
  DipSwitch dipswitch_8 (.out(dipswitch_8_out));
  or or_13 (or_13_out, and_26_out, and_27_out);
  or or_14 (or_14_out, and_28_out, and_29_out);
  or or_15 (or_15_out, and_30_out, and_31_out);
  or or_16 (or_16_out, and_32_out, and_33_out);
  _74189 _74189_1 (
    .pin1(or_16_out), .pin2(_74189_1_pin2), .pin3(not_1_out), .pin4(or_12_out), .pin5(_74189_1_pin5),
    .pin6(or_11_out), .pin7(_74189_1_pin7), .pin8(1'b0), .pin9(_74189_1_pin9), .pin10(or_10_out),
    .pin11(_74189_1_pin11), .pin12(or_9_out), .pin13(or_13_out), .pin14(or_14_out), .pin15(or_15_out),
    .pin16(1'b1));
  not not_12 (_74189_1_pin2, 1'b1);
  not not_13 (not_13_out, _74189_1_pin11);
  not not_14 (not_14_out, _74189_1_pin9);
  not not_15 (not_15_out, _74189_1_pin7);
  not not_16 (not_16_out, _74189_1_pin5);
  Tri_State_Buffer tri_state_buffer_1 (.IN(not_13_out), .EN(and_1_out), .OUT(tri_state_buffer_1_out));
  Tri_State_Buffer tri_state_buffer_2 (.IN(not_15_out), .EN(and_1_out), .OUT(tri_state_buffer_2_out));
  Tri_State_Buffer tri_state_buffer_3 (.IN(not_14_out), .EN(and_1_out), .OUT(tri_state_buffer_3_out));
  Tri_State_Buffer tri_state_buffer_4 (.IN(not_16_out), .EN(and_1_out), .OUT(tri_state_buffer_4_out));
  DipSwitch dipswitch_9 (.out(tri_state_buffer_1_out));
  DipSwitch dipswitch_10 (.out(tri_state_buffer_3_out));
  DipSwitch dipswitch_11 (.out(tri_state_buffer_2_out));
  DipSwitch dipswitch_12 (.out(tri_state_buffer_4_out));

  // Notes on the sheet:
  //   SEL: Dip and BUS
  //   SEL_2: Dip and BUS
  //   MAR
  //   MDR
  //   BUS
  //   3
  //   2
  //   1
  //   0
  //   CLK
  //   GND
  //   5V
endmodule
