// Digital circuit ALU_with_Flags_IC.dig as structural Verilog
module ALU_with_Flags_IC (
  input  A1,
  input  A2,
  input  A3,
  input  A4,
  input  B1,
  input  B2,
  input  B3,
  input  B4,
  input  SU,
  input  EN,
  input  CLK,
  output CAR,
  output _1,
  output _2,
  output _3,
  output _4,
  output NEG,
  output Z
);

  wire _3_STATE_pin1, AND_2_pin3, AND_2_pin6, AND_2_pin8, AND_2_pin11, AND_3_pin1, AND_3_pin2, AND_3_pin3,
       AND_3_pin5, AND_3_pin6, AND_3_pin10, AND_pin3, AND_pin6, AND_pin8, AND_pin11, XOR_2_pin3, XOR_2_pin5,
       XOR_2_pin6, XOR_2_pin9, XOR_2_pin10, XOR_3_pin3, XOR_3_pin6, XOR_3_pin8, XOR_3_pin9, XOR_3_pin10,
       XOR_pin3, XOR_pin6, XOR_pin8, XOR_pin11;

  _7486 XOR (
    .pin1(SU), .pin2(B1), .pin3(XOR_pin3), .pin4(SU), .pin5(B2), .pin6(XOR_pin6), .pin7(1'b0),
    .pin8(XOR_pin8), .pin9(SU), .pin10(B3), .pin11(XOR_pin11), .pin12(SU), .pin13(B4), .pin14(1'b1));
  _7486 XOR_2 (
    .pin1(A3), .pin2(XOR_pin8), .pin3(XOR_2_pin3), .pin4(XOR_2_pin3), .pin5(XOR_2_pin5), .pin6(XOR_2_pin6),
    .pin7(1'b0), .pin8(NEG), .pin9(XOR_2_pin9), .pin10(XOR_2_pin10), .pin11(XOR_2_pin10), .pin12(A4),
    .pin13(XOR_pin11), .pin14(1'b1));
  _7408 AND (
    .pin1(A3), .pin2(XOR_pin8), .pin3(AND_pin3), .pin4(XOR_2_pin3), .pin5(XOR_2_pin5), .pin6(AND_pin6),
    .pin7(1'b0), .pin8(AND_pin8), .pin9(XOR_2_pin9), .pin10(XOR_2_pin10), .pin11(AND_pin11), .pin12(A4),
    .pin13(XOR_pin11), .pin14(1'b1));
  _7486 XOR_3 (
    .pin1(A1), .pin2(XOR_pin3), .pin3(XOR_3_pin3), .pin4(XOR_3_pin3), .pin5(SU), .pin6(XOR_3_pin6),
    .pin7(1'b0), .pin8(XOR_3_pin8), .pin9(XOR_3_pin9), .pin10(XOR_3_pin10), .pin11(XOR_3_pin10), .pin12(A2),
    .pin13(XOR_pin6), .pin14(1'b1));
  _7408 AND_2 (
    .pin1(A1), .pin2(XOR_pin3), .pin3(AND_2_pin3), .pin4(SU), .pin5(XOR_3_pin3), .pin6(AND_2_pin6),
    .pin7(1'b0), .pin8(AND_2_pin8), .pin9(XOR_3_pin9), .pin10(XOR_3_pin10), .pin11(AND_2_pin11), .pin12(A2),
    .pin13(XOR_pin6), .pin14(1'b1));
  _7432 OR (
    .pin1(AND_2_pin6), .pin2(AND_2_pin3), .pin3(XOR_3_pin9), .pin4(AND_2_pin8), .pin5(AND_2_pin11),
    .pin6(XOR_2_pin5), .pin7(1'b0), .pin8(XOR_2_pin9), .pin9(AND_pin6), .pin10(AND_pin3), .pin11(CAR),
    .pin12(AND_pin8), .pin13(AND_pin11), .pin14(1'b1));
  _74126 _3_STATE (
    .pin1(_3_STATE_pin1), .pin2(XOR_3_pin6), .pin3(_1), .pin4(_3_STATE_pin1), .pin5(XOR_3_pin8), .pin6(_2),
    .pin7(1'b0), .pin8(_3), .pin9(XOR_2_pin6), .pin10(_3_STATE_pin1), .pin11(_4), .pin12(NEG),
    .pin13(_3_STATE_pin1), .pin14(1'b1));
  _7408 AND_3 (
    .pin1(AND_3_pin1), .pin2(AND_3_pin2), .pin3(AND_3_pin3), .pin4(AND_3_pin3), .pin5(AND_3_pin5),
    .pin6(AND_3_pin6), .pin7(1'b0), .pin8(Z), .pin9(AND_3_pin6), .pin10(AND_3_pin10), .pin11(_3_STATE_pin1),
    .pin12(CLK), .pin13(EN), .pin14(1'b1));
  _7404 NOT (
    .pin1(XOR_3_pin6), .pin2(AND_3_pin1), .pin3(1'b0), .pin5(1'b0), .pin7(1'b0), .pin8(AND_3_pin10),
    .pin9(NEG), .pin10(AND_3_pin5), .pin11(XOR_2_pin6), .pin12(AND_3_pin2), .pin13(XOR_3_pin8), .pin14(1'b1));  // open: pin4, pin6

  // Notes on the sheet:
  //   Output
endmodule
