// Digital circuit Full_Assembly.dig as structural Verilog
module Full_Assembly (
  input  CLR_A,
  input  CLR_B,
  input  in_6,
  input  CLR_IR,
  input  MAR_IN,
  input  RAM_IN,
  input  RAM_OUT,
  input  IR_OUT,
  input  IR_IN,
  input  A_IN,
  input  A_OUT,
  input  B_IN,
  input  B_OUT,
  input  ALU_OUT,
  input  SUB_EN,
  input  OREG_IN,
  input  CNT_EN,
  input  JMP,
  input  PC_OUT,
  input  CLR,
  input  SEL,
  input  CLR_2,
  input  in_26,
  input  in_27,
  input  in_28,
  input  in_29,
  output Z,
  output CAR,
  output NEG
);

  wire _3_STATE_5_pin1, _3_STATE_pin1, _28c16_1_p15, _28c16_1_p16, _28c16_1_p17, _28c16_1_p18, _28c16_2_p2,
       _28c16_2_p3, _28c16_2_p17, _28c16_2_p19, _28c16_2_p20, _28c16_2_p21, _28c16_2_p22, _28c16_2_p23,
       _7489_1_pin1, _7489_1_pin3, _7489_1_pin4, _7489_1_pin5, _7489_1_pin6, _7489_1_pin7, _7489_1_pin9,
       _7489_1_pin10, _7489_1_pin11, _7489_1_pin12, _7489_1_pin13, _7489_1_pin14, _7489_1_pin15,
       _7489_2_pin4, _7489_2_pin5, _7489_2_pin6, _7489_2_pin7, _7489_2_pin9, _7489_2_pin10, _7489_2_pin11,
       _7489_2_pin12, _74163_1_pin2, _74163_1_pin12, _74163_1_pin13, _74163_1_pin14, _74163_2_pin9,
       _74163_2_pin11, _74163_2_pin12, _74163_2_pin13, _74163_2_pin14, _74283_1_pin1, _74283_1_pin4,
       _74283_1_pin13, AND_2_pin3, AND_2_pin6, AND_pin1, D_3_OUT_2_pin3, D_3_OUT_2_pin4, D_3_OUT_2_pin5,
       D_3_OUT_2_pin6, D_3_OUT_2_pin9, D_3_OUT_2_pin11, D_3_OUT_2_pin12, D_3_OUT_2_pin13, D_3_OUT_2_pin14,
       D_3_OUT_3_pin3, D_3_OUT_3_pin4, D_3_OUT_3_pin5, D_3_OUT_3_pin6, D_3_OUT_4_pin3, D_3_OUT_4_pin4,
       D_3_OUT_4_pin5, D_3_OUT_4_pin6, D_3_OUT_4_pin9, D_3_OUT_5_pin3, D_3_OUT_5_pin4, D_3_OUT_5_pin5,
       D_3_OUT_5_pin6, D_3_OUT_5_pin9, D_3_OUT_6_pin3, D_3_OUT_6_pin4, D_3_OUT_6_pin5, D_3_OUT_6_pin6,
       D_3_OUT_6_pin9, D_3_OUT_7_pin3, D_3_OUT_7_pin4, D_3_OUT_7_pin5, D_3_OUT_7_pin6, D_3_OUT_pin3,
       D_3_OUT_pin4, D_3_OUT_pin5, D_3_OUT_pin6, MUX_2_pin3, MUX_2_pin6, MUX_2_pin10, MUX_2_pin13, MUX_pin3,
       MUX_pin6, MUX_pin10, MUX_pin13, NOT_2_pin2, NOT_2_pin4, NOT_2_pin10, NOT_2_pin12, NOT_4_pin2,
       NOT_4_pin4, NOT_4_pin6, NOT_4_pin8, NOT_5_pin4, NOT_pin2, NOT_pin4, NOT_pin10, NOT_pin12, XOR_pin1,
       XOR_pin3, XOR_pin6, XOR_pin8, XOR_pin11;

  _7489 _7489_1 (
    .pin1(_7489_1_pin1), .pin2(1'b0), .pin3(_7489_1_pin3), .pin4(_7489_1_pin4), .pin5(_7489_1_pin5),
    .pin6(_7489_1_pin6), .pin7(_7489_1_pin7), .pin8(1'b0), .pin9(_7489_1_pin9), .pin10(_7489_1_pin10),
    .pin11(_7489_1_pin11), .pin12(_7489_1_pin12), .pin13(_7489_1_pin13), .pin14(_7489_1_pin14),
    .pin15(_7489_1_pin15), .pin16(1'b1));
  _74163 _74163_1 (
    .pin1(1'b1), .pin2(_74163_1_pin2), .pin3(in_26), .pin4(in_27), .pin5(in_28), .pin6(in_29), .pin7(1'b1),
    .pin8(1'b0), .pin9(1'b1), .pin10(1'b1), .pin12(_74163_1_pin12), .pin13(_74163_1_pin13),
    .pin14(_74163_1_pin14), .pin16(1'b1));  // open: pin11, pin15
  LED led_1 (.in(NOT_pin2));
  LED led_2 (.in(NOT_pin4));
  _7404 NOT (
    .pin1(_7489_1_pin5), .pin2(NOT_pin2), .pin3(_7489_1_pin7), .pin4(NOT_pin4), .pin5(1'b0), .pin7(1'b0),
    .pin9(1'b0), .pin10(NOT_pin10), .pin11(_7489_1_pin9), .pin12(NOT_pin12), .pin13(_7489_1_pin11),
    .pin14(1'b1));  // open: pin6, pin8
  LED led_3 (.in(NOT_pin10));
  LED led_4 (.in(NOT_pin12));
  LED led_5 (.in(NOT_2_pin2));
  LED led_6 (.in(NOT_2_pin4));
  LED led_7 (.in(NOT_2_pin10));
  LED led_8 (.in(NOT_2_pin12));
  _74138 _74138_1 (
    .pin1(_74163_1_pin14), .pin2(_74163_1_pin13), .pin3(_74163_1_pin12), .pin4(1'b0), .pin5(1'b0),
    .pin6(1'b1), .pin8(1'b0), .pin16(1'b1));  // open: pin7, pin9, pin10, pin11, pin12, pin13, pin14, pin15
  _74173 D_3_OUT (
    .pin1(1'b0), .pin2(1'b0), .pin3(D_3_OUT_pin3), .pin4(D_3_OUT_pin4), .pin5(D_3_OUT_pin5),
    .pin6(D_3_OUT_pin6), .pin7(in_6), .pin8(1'b0), .pin9(1'b0), .pin10(1'b0), .pin11(NOT_pin12),
    .pin12(NOT_pin10), .pin13(NOT_pin4), .pin14(NOT_pin2), .pin15(CLR_IR), .pin16(1'b1));
  _74173 D_3_OUT_2 (
    .pin1(1'b0), .pin2(1'b0), .pin3(D_3_OUT_2_pin3), .pin4(D_3_OUT_2_pin4), .pin5(D_3_OUT_2_pin5),
    .pin6(D_3_OUT_2_pin6), .pin7(in_6), .pin8(1'b0), .pin9(D_3_OUT_2_pin9), .pin10(D_3_OUT_2_pin9),
    .pin11(D_3_OUT_2_pin11), .pin12(D_3_OUT_2_pin12), .pin13(D_3_OUT_2_pin13), .pin14(D_3_OUT_2_pin14),
    .pin15(CLR), .pin16(1'b1));
  _7489 _7489_2 (
    .pin1(_7489_1_pin1), .pin2(1'b0), .pin3(_7489_1_pin3), .pin4(_7489_2_pin4), .pin5(_7489_2_pin5),
    .pin6(_7489_2_pin6), .pin7(_7489_2_pin7), .pin8(1'b0), .pin9(_7489_2_pin9), .pin10(_7489_2_pin10),
    .pin11(_7489_2_pin11), .pin12(_7489_2_pin12), .pin13(_7489_1_pin13), .pin14(_7489_1_pin14),
    .pin15(_7489_1_pin15), .pin16(1'b1));
  _74173 D_3_OUT_3 (
    .pin1(1'b0), .pin2(1'b0), .pin3(D_3_OUT_3_pin3), .pin4(D_3_OUT_3_pin4), .pin5(D_3_OUT_3_pin5),
    .pin6(D_3_OUT_3_pin6), .pin7(in_6), .pin8(1'b0), .pin9(D_3_OUT_2_pin9), .pin10(D_3_OUT_2_pin9),
    .pin11(D_3_OUT_2_pin11), .pin12(D_3_OUT_2_pin12), .pin13(D_3_OUT_2_pin13), .pin14(D_3_OUT_2_pin14),
    .pin15(CLR_2), .pin16(1'b1));
  // _28c16 _28c16_1: pin names not known; wires that end beside it: 1'b0, 1'b0, D_3_OUT_pin6, 1'b0, D_3_OUT_pin5, 1'b1, D_3_OUT_pin4, 1'b0, D_3_OUT_pin3, 1'b0, _74163_1_pin12, 1'b0, _74163_1_pin13, _74163_1_pin14, _28c16_1_p15, _28c16_1_p16, _28c16_1_p17, _28c16_1_p18
  LED led_9 (.in(D_3_OUT_2_pin6));
  LED led_10 (.in(D_3_OUT_2_pin5));
  LED led_11 (.in(_3_STATE_pin1));
  LED led_12 (.in(D_3_OUT_pin6));
  LED led_13 (.in(D_3_OUT_2_pin3));
  _74173 D_3_OUT_4 (
    .pin1(1'b0), .pin2(1'b0), .pin3(D_3_OUT_4_pin3), .pin4(D_3_OUT_4_pin4), .pin5(D_3_OUT_4_pin5),
    .pin6(D_3_OUT_4_pin6), .pin7(in_6), .pin8(1'b0), .pin9(D_3_OUT_4_pin9), .pin10(D_3_OUT_4_pin9),
    .pin11(D_3_OUT_2_pin11), .pin12(D_3_OUT_2_pin12), .pin13(D_3_OUT_2_pin13), .pin14(D_3_OUT_2_pin14),
    .pin15(CLR_IR), .pin16(1'b1));
  LED led_14 (.in(D_3_OUT_pin5));
  LED led_15 (.in(D_3_OUT_pin4));
  _74157 MUX (
    .pin1(SEL), .pin2(D_3_OUT_2_pin3), .pin3(MUX_pin3), .pin4(_7489_1_pin1), .pin5(D_3_OUT_2_pin4),
    .pin6(MUX_pin6), .pin7(_7489_1_pin15), .pin8(1'b0), .pin9(_7489_1_pin14), .pin10(MUX_pin10),
    .pin11(D_3_OUT_2_pin5), .pin12(_7489_1_pin13), .pin13(MUX_pin13), .pin14(D_3_OUT_2_pin6), .pin15(1'b0),
    .pin16(1'b1));
  _7404 NOT_2 (
    .pin1(_7489_2_pin5), .pin2(NOT_2_pin2), .pin3(_7489_2_pin7), .pin4(NOT_2_pin4), .pin5(1'b0), .pin7(1'b0),
    .pin9(1'b0), .pin10(NOT_2_pin10), .pin11(_7489_2_pin9), .pin12(NOT_2_pin12), .pin13(_7489_2_pin11),
    .pin14(1'b1));  // open: pin6, pin8
  _74157 MUX_2 (
    .pin1(SEL), .pin2(D_3_OUT_3_pin3), .pin3(MUX_2_pin3), .pin4(_7489_2_pin4), .pin5(D_3_OUT_3_pin4),
    .pin6(MUX_2_pin6), .pin7(_7489_2_pin6), .pin8(1'b0), .pin9(_7489_2_pin10), .pin10(MUX_2_pin10),
    .pin11(D_3_OUT_3_pin5), .pin12(_7489_2_pin12), .pin13(MUX_2_pin13), .pin14(D_3_OUT_3_pin6), .pin15(1'b0),
    .pin16(1'b1));
  LED led_16 (.in(D_3_OUT_pin3));
  LED led_17 (.in(D_3_OUT_4_pin6));
  LED led_18 (.in(D_3_OUT_4_pin5));
  LED led_19 (.in(D_3_OUT_4_pin4));
  LED led_20 (.in(D_3_OUT_4_pin3));
  _74126 _3_STATE (
    .pin1(_3_STATE_pin1), .pin2(NOT_2_pin2), .pin3(D_3_OUT_2_pin14), .pin4(_3_STATE_pin1), .pin5(NOT_2_pin4),
    .pin6(D_3_OUT_2_pin13), .pin7(1'b0), .pin8(D_3_OUT_2_pin12), .pin9(NOT_2_pin10), .pin10(_3_STATE_pin1),
    .pin11(D_3_OUT_2_pin11), .pin12(NOT_2_pin12), .pin13(_3_STATE_pin1), .pin14(1'b1));
  _74126 _3_STATE_2 (
    .pin1(_28c16_1_p16), .pin2(D_3_OUT_4_pin3), .pin3(D_3_OUT_2_pin14), .pin4(_28c16_1_p16),
    .pin5(D_3_OUT_4_pin4), .pin6(D_3_OUT_2_pin13), .pin7(1'b0), .pin8(D_3_OUT_2_pin12),
    .pin9(D_3_OUT_4_pin5), .pin10(_28c16_1_p16), .pin11(D_3_OUT_2_pin11), .pin12(D_3_OUT_4_pin6),
    .pin13(_28c16_1_p16), .pin14(1'b1));
  // _28c16 _28c16_2: pin names not known; wires that end beside it: _3_STATE_pin1, _28c16_2_p2, _28c16_2_p3, 1'b0, 1'b0, D_3_OUT_pin6, 1'b0, D_3_OUT_pin5, 1'b1, D_3_OUT_pin4, 1'b0, D_3_OUT_pin3, 1'b0, _74163_1_pin12, 1'b0, _74163_1_pin13, _28c16_2_p17, _74163_1_pin14, _28c16_2_p19, _28c16_2_p20, _28c16_2_p21, _28c16_2_p22, _28c16_2_p23
  DipSwitch dipswitch_1 (.out(MUX_pin13));
  DipSwitch dipswitch_2 (.out(MUX_pin10));
  DipSwitch dipswitch_3 (.out(MUX_pin6));
  DipSwitch dipswitch_4 (.out(MUX_pin3));
  DipSwitch dipswitch_5 (.out(_7489_1_pin12));
  DipSwitch dipswitch_6 (.out(_7489_1_pin10));
  DipSwitch dipswitch_7 (.out(_7489_1_pin6));
  DipSwitch dipswitch_8 (.out(_7489_1_pin4));
  DipSwitch dipswitch_9 (.out(MUX_2_pin13));
  DipSwitch dipswitch_10 (.out(MUX_2_pin10));
  DipSwitch dipswitch_11 (.out(MUX_2_pin6));
  DipSwitch dipswitch_12 (.out(MUX_2_pin3));
  _7404 NOT_3 (
    .pin1(1'b1), .pin3(1'b1), .pin5(1'b1), .pin7(1'b0), .pin8(_74163_1_pin2), .pin9(in_6), .pin11(1'b1),
    .pin13(1'b1), .pin14(1'b1));  // open: pin2, pin4, pin6, pin10, pin12
  _7408 AND (
    .pin1(AND_pin1), .pin2(in_6), .pin3(_7489_1_pin3), .pin4(1'b0), .pin5(1'b0), .pin7(1'b0), .pin9(1'b1),
    .pin10(1'b1), .pin12(1'b1), .pin13(1'b1), .pin14(1'b1));  // open: pin6, pin8, pin11
  _7486 XOR (
    .pin1(XOR_pin1), .pin2(D_3_OUT_2_pin14), .pin3(XOR_pin3), .pin4(XOR_pin1), .pin5(D_3_OUT_2_pin13),
    .pin6(XOR_pin6), .pin7(1'b0), .pin8(XOR_pin8), .pin9(XOR_pin1), .pin10(D_3_OUT_2_pin12),
    .pin11(XOR_pin11), .pin12(XOR_pin1), .pin13(D_3_OUT_2_pin11), .pin14(1'b1));
  _74163 _74163_2 (
    .pin1(1'b1), .pin2(in_6), .pin3(D_3_OUT_2_pin14), .pin4(D_3_OUT_2_pin13), .pin5(D_3_OUT_2_pin12),
    .pin6(D_3_OUT_2_pin11), .pin7(_28c16_2_p23), .pin8(1'b0), .pin9(_74163_2_pin9), .pin10(_28c16_2_p23),
    .pin11(_74163_2_pin11), .pin12(_74163_2_pin12), .pin13(_74163_2_pin13), .pin14(_74163_2_pin14),
    .pin16(1'b1));  // open: pin15
  _74173 D_3_OUT_5 (
    .pin1(1'b0), .pin2(1'b0), .pin3(D_3_OUT_5_pin3), .pin4(D_3_OUT_5_pin4), .pin5(D_3_OUT_5_pin5),
    .pin6(D_3_OUT_5_pin6), .pin7(in_6), .pin8(1'b0), .pin9(D_3_OUT_5_pin9), .pin10(D_3_OUT_5_pin9),
    .pin11(D_3_OUT_2_pin11), .pin12(D_3_OUT_2_pin12), .pin13(D_3_OUT_2_pin13), .pin14(D_3_OUT_2_pin14),
    .pin15(CLR_A), .pin16(1'b1));
  _74173 D_3_OUT_6 (
    .pin1(1'b0), .pin2(1'b0), .pin3(D_3_OUT_6_pin3), .pin4(D_3_OUT_6_pin4), .pin5(D_3_OUT_6_pin5),
    .pin6(D_3_OUT_6_pin6), .pin7(in_6), .pin8(1'b0), .pin9(D_3_OUT_6_pin9), .pin10(D_3_OUT_6_pin9),
    .pin11(D_3_OUT_2_pin11), .pin12(D_3_OUT_2_pin12), .pin13(D_3_OUT_2_pin13), .pin14(D_3_OUT_2_pin14),
    .pin15(1'b0), .pin16(1'b1));
  LED led_21 (.in(_74163_2_pin11));
  LED led_22 (.in(_74163_2_pin12));
  LED led_23 (.in(D_3_OUT_5_pin3));
  LED led_24 (.in(D_3_OUT_5_pin4));
  LED led_25 (.in(_74163_2_pin13));
  LED led_26 (.in(_74163_2_pin14));
  LED led_27 (.in(D_3_OUT_5_pin5));
  LED led_28 (.in(D_3_OUT_5_pin6));
  _74283 _74283_1 (
    .pin1(_74283_1_pin1), .pin2(XOR_pin6), .pin3(D_3_OUT_2_pin13), .pin4(_74283_1_pin4),
    .pin5(D_3_OUT_2_pin14), .pin6(XOR_pin3), .pin7(XOR_pin1), .pin8(1'b0), .pin9(CAR), .pin10(NEG),
    .pin11(XOR_pin11), .pin12(D_3_OUT_2_pin11), .pin13(_74283_1_pin13), .pin14(D_3_OUT_2_pin12),
    .pin15(XOR_pin8), .pin16(1'b1));
  LED led_29 (.in(_74283_1_pin4));
  _74126 _3_STATE_3 (
    .pin1(_28c16_2_p20), .pin2(_74163_2_pin14), .pin3(D_3_OUT_2_pin14), .pin4(_28c16_2_p20),
    .pin5(_74163_2_pin13), .pin6(D_3_OUT_2_pin13), .pin7(1'b0), .pin8(D_3_OUT_2_pin12),
    .pin9(_74163_2_pin12), .pin10(_28c16_2_p20), .pin11(D_3_OUT_2_pin11), .pin12(_74163_2_pin11),
    .pin13(_28c16_2_p20), .pin14(1'b1));
  LED led_30 (.in(_74283_1_pin1));
  LED led_31 (.in(_74283_1_pin13));
  _74126 _3_STATE_4 (
    .pin1(_28c16_2_p2), .pin2(D_3_OUT_5_pin3), .pin3(D_3_OUT_2_pin14), .pin4(_28c16_2_p2),
    .pin5(D_3_OUT_5_pin4), .pin6(D_3_OUT_2_pin13), .pin7(1'b0), .pin8(D_3_OUT_2_pin12),
    .pin9(D_3_OUT_5_pin5), .pin10(_28c16_2_p2), .pin11(D_3_OUT_2_pin11), .pin12(D_3_OUT_5_pin6),
    .pin13(_28c16_2_p2), .pin14(1'b1));
  LED led_32 (.in(NEG));
  _74126 _3_STATE_5 (
    .pin1(_3_STATE_5_pin1), .pin2(_74283_1_pin4), .pin3(D_3_OUT_2_pin14), .pin4(_3_STATE_5_pin1),
    .pin5(_74283_1_pin1), .pin6(D_3_OUT_2_pin13), .pin7(1'b0), .pin8(D_3_OUT_2_pin12), .pin9(_74283_1_pin13),
    .pin10(_3_STATE_5_pin1), .pin11(D_3_OUT_2_pin11), .pin12(NEG), .pin13(_3_STATE_5_pin1), .pin14(1'b1));
  LED led_33 (.in(D_3_OUT_6_pin6));
  LED led_34 (.in(D_3_OUT_6_pin5));
  LED led_35 (.in(D_3_OUT_6_pin4));
  LED led_36 (.in(D_3_OUT_6_pin3));
  _7404 NOT_4 (
    .pin1(_74283_1_pin4), .pin2(NOT_4_pin2), .pin3(_74283_1_pin1), .pin4(NOT_4_pin4), .pin5(_74283_1_pin13),
    .pin6(NOT_4_pin6), .pin7(1'b0), .pin8(NOT_4_pin8), .pin9(NEG), .pin11(1'b1), .pin13(1'b1), .pin14(1'b1));  // open: pin10, pin12
  _7404 NOT_5 (
    .pin1(_28c16_2_p22), .pin2(_74163_2_pin9), .pin3(_28c16_2_p17), .pin4(NOT_5_pin4), .pin5(_28c16_1_p18),
    .pin6(D_3_OUT_5_pin9), .pin7(1'b0), .pin8(D_3_OUT_4_pin9), .pin9(_28c16_2_p3), .pin10(AND_pin1),
    .pin11(_28c16_1_p17), .pin12(D_3_OUT_2_pin9), .pin13(_28c16_1_p15), .pin14(1'b1));
  _74173 D_3_OUT_7 (
    .pin1(1'b0), .pin2(1'b0), .pin3(D_3_OUT_7_pin3), .pin4(D_3_OUT_7_pin4), .pin5(D_3_OUT_7_pin5),
    .pin6(D_3_OUT_7_pin6), .pin7(in_6), .pin8(1'b0), .pin9(NOT_5_pin4), .pin10(NOT_5_pin4),
    .pin11(D_3_OUT_2_pin11), .pin12(D_3_OUT_2_pin12), .pin13(D_3_OUT_2_pin13), .pin14(D_3_OUT_2_pin14),
    .pin15(CLR_B), .pin16(1'b1));
  LED led_37 (.in(D_3_OUT_7_pin3));
  LED led_38 (.in(D_3_OUT_7_pin4));
  LED led_39 (.in(D_3_OUT_7_pin5));
  _7408 AND_2 (
    .pin1(NOT_4_pin2), .pin2(NOT_4_pin4), .pin3(AND_2_pin3), .pin4(AND_2_pin3), .pin5(NOT_4_pin6),
    .pin6(AND_2_pin6), .pin7(1'b0), .pin8(Z), .pin9(AND_2_pin6), .pin10(NOT_4_pin8), .pin11(_3_STATE_5_pin1),
    .pin12(in_6), .pin13(_28c16_2_p21), .pin14(1'b1));
  LED led_40 (.in(D_3_OUT_7_pin6));
  _74126 _3_STATE_6 (
    .pin1(_28c16_2_p19), .pin2(D_3_OUT_7_pin3), .pin3(D_3_OUT_2_pin14), .pin4(_28c16_2_p19),
    .pin5(D_3_OUT_7_pin4), .pin6(D_3_OUT_2_pin13), .pin7(1'b0), .pin8(D_3_OUT_2_pin12),
    .pin9(D_3_OUT_7_pin5), .pin10(_28c16_2_p19), .pin11(D_3_OUT_2_pin11), .pin12(D_3_OUT_7_pin6),
    .pin13(_28c16_2_p19), .pin14(1'b1));

  // Notes on the sheet:
  //   RAM Module
  //   MDR
  //   MAR
  //   IR
  //   4
  //   3
  //   2
  //   1
  //   CLK
  //   5V
  //   GND
  //   PC
  //   A and B Reg
  //   ALU
  //   OUT Reg
endmodule
