// Digital circuit RAM_MAR_MDR_IC.dig as structural Verilog
module RAM_MAR_MDR_IC (
  input  EN,
  input  CLK,
  input  SEL,
  input  CLR,
  input  A1,
  input  A2,
  input  A3,
  input  A4,
  input  SEL_2,
  input  D1,
  input  D2,
  input  D3,
  input  D4,
  input  CLR_2,
  input  LOAD,
  output O1,
  output O2,
  output O3,
  output O4
);

  wire D_3_OUT_2_pin3, D_3_OUT_2_pin4, D_3_OUT_2_pin5, D_3_OUT_2_pin6, D_3_OUT_pin3, D_3_OUT_pin4,
       D_3_OUT_pin5, D_3_OUT_pin6, MUX_2_pin3, MUX_2_pin6, MUX_2_pin10, MUX_2_pin13, MUX_pin3, MUX_pin6,
       MUX_pin10, MUX_pin13, NOT_pin2, NOT_pin4, NOT_pin10, NOT_pin12, SRAM_pin1, SRAM_pin3, SRAM_pin4,
       SRAM_pin5, SRAM_pin6, SRAM_pin7, SRAM_pin9, SRAM_pin10, SRAM_pin11, SRAM_pin12, SRAM_pin13,
       SRAM_pin14, SRAM_pin15, W_out;

  Button #(.activeLow("true")) W (.out(W_out));
  _74173 D_3_OUT (
    .pin1(1'b0), .pin2(1'b0), .pin3(D_3_OUT_pin3), .pin4(D_3_OUT_pin4), .pin5(D_3_OUT_pin5),
    .pin6(D_3_OUT_pin6), .pin7(CLK), .pin8(1'b0), .pin9(LOAD), .pin10(LOAD), .pin11(A4), .pin12(A3),
    .pin13(A2), .pin14(A1), .pin15(CLR), .pin16(1'b1));
  _74189 SRAM (
    .pin1(SRAM_pin1), .pin2(1'b0), .pin3(SRAM_pin3), .pin4(SRAM_pin4), .pin5(SRAM_pin5), .pin6(SRAM_pin6),
    .pin7(SRAM_pin7), .pin8(1'b0), .pin9(SRAM_pin9), .pin10(SRAM_pin10), .pin11(SRAM_pin11),
    .pin12(SRAM_pin12), .pin13(SRAM_pin13), .pin14(SRAM_pin14), .pin15(SRAM_pin15), .pin16(1'b1));
  _74173 D_3_OUT_2 (
    .pin1(1'b0), .pin2(1'b0), .pin3(D_3_OUT_2_pin3), .pin4(D_3_OUT_2_pin4), .pin5(D_3_OUT_2_pin5),
    .pin6(D_3_OUT_2_pin6), .pin7(CLK), .pin8(1'b0), .pin9(LOAD), .pin10(LOAD), .pin11(D4), .pin12(D3),
    .pin13(D2), .pin14(D1), .pin15(CLR_2), .pin16(1'b1));
  _74157 MUX (
    .pin1(SEL), .pin2(D_3_OUT_pin3), .pin3(MUX_pin3), .pin4(SRAM_pin1), .pin5(D_3_OUT_pin4), .pin6(MUX_pin6),
    .pin7(SRAM_pin15), .pin8(1'b0), .pin9(SRAM_pin14), .pin10(MUX_pin10), .pin11(D_3_OUT_pin5),
    .pin12(SRAM_pin13), .pin13(MUX_pin13), .pin14(D_3_OUT_pin6), .pin15(1'b0), .pin16(1'b1));
  _7404 NOT (
    .pin1(SRAM_pin5), .pin2(NOT_pin2), .pin3(SRAM_pin7), .pin4(NOT_pin4), .pin5(1'b0), .pin7(1'b0),
    .pin9(1'b0), .pin10(NOT_pin10), .pin11(SRAM_pin9), .pin12(NOT_pin12), .pin13(SRAM_pin11), .pin14(1'b1));  // open: pin6, pin8
  _74157 MUX_2 (
    .pin1(SEL_2), .pin2(D_3_OUT_2_pin3), .pin3(MUX_2_pin3), .pin4(SRAM_pin4), .pin5(D_3_OUT_2_pin4),
    .pin6(MUX_2_pin6), .pin7(SRAM_pin6), .pin8(1'b0), .pin9(SRAM_pin10), .pin10(MUX_2_pin10),
    .pin11(D_3_OUT_2_pin5), .pin12(SRAM_pin12), .pin13(MUX_2_pin13), .pin14(D_3_OUT_2_pin6), .pin15(1'b0),
    .pin16(1'b1));
  _74126 _3_STATE (
    .pin1(EN), .pin2(NOT_pin2), .pin3(O1), .pin4(EN), .pin5(NOT_pin4), .pin6(O2), .pin7(1'b0), .pin8(O3),
    .pin9(NOT_pin10), .pin10(EN), .pin11(O4), .pin12(NOT_pin12), .pin13(EN), .pin14(1'b1));
  DipSwitch dipswitch_1 (.out(MUX_pin13));
  DipSwitch dipswitch_2 (.out(MUX_pin10));
  DipSwitch dipswitch_3 (.out(MUX_pin6));
  DipSwitch dipswitch_4 (.out(MUX_pin3));
  DipSwitch dipswitch_5 (.out(MUX_2_pin13));
  DipSwitch dipswitch_6 (.out(MUX_2_pin10));
  DipSwitch dipswitch_7 (.out(MUX_2_pin6));
  DipSwitch dipswitch_8 (.out(MUX_2_pin3));
  _7408 AND (
    .pin1(W_out), .pin2(CLK), .pin3(SRAM_pin3), .pin4(1'b0), .pin5(1'b0), .pin7(1'b0), .pin9(1'b1),
    .pin10(1'b1), .pin12(1'b1), .pin13(1'b1), .pin14(1'b1));  // open: pin6, pin8, pin11

  // Notes on the sheet:
  //   MAR
  //   RAM Module
  //   MDR
endmodule
