// Digital circuit RAM_Module_8-bit_IC.dig as structural Verilog
module RAM_Module_8_bit_IC (
  input  EN,
  input  CLK,
  input  SEL,
  input  CLR,
  input  A1,
  input  A2,
  input  A3,
  input  A4,
  input  SEL_2,
  input  D1,
  input  D2,
  input  D3,
  input  D4,
  input  CLR_2,
  input  LOAD,
  input  WE,
  output O1,
  output O2,
  output O3,
  output O4
);

  wire _7489_1_pin1, _7489_1_pin4, _7489_1_pin5, _7489_1_pin6, _7489_1_pin7, _7489_1_pin9, _7489_1_pin10,
       _7489_1_pin11, _7489_1_pin12, _7489_1_pin13, _7489_1_pin14, _7489_1_pin15, _7489_2_pin4, _7489_2_pin5,
       _7489_2_pin6, _7489_2_pin7, _7489_2_pin9, _7489_2_pin10, _7489_2_pin11, _7489_2_pin12, D_3_OUT_2_pin3,
       D_3_OUT_2_pin4, D_3_OUT_2_pin5, D_3_OUT_2_pin6, D_3_OUT_pin3, D_3_OUT_pin4, D_3_OUT_pin5,
       D_3_OUT_pin6, MUX_2_pin3, MUX_2_pin6, MUX_2_pin10, MUX_2_pin13, MUX_pin3, MUX_pin6, MUX_pin10,
       MUX_pin13, NOT_2_pin2, NOT_2_pin4, NOT_2_pin10, NOT_2_pin12, NOT_pin2, NOT_pin4, NOT_pin10, NOT_pin12;

  _7489 _7489_1 (
    .pin1(_7489_1_pin1), .pin2(1'b0), .pin3(WE), .pin4(_7489_1_pin4), .pin5(_7489_1_pin5),
    .pin6(_7489_1_pin6), .pin7(_7489_1_pin7), .pin8(1'b0), .pin9(_7489_1_pin9), .pin10(_7489_1_pin10),
    .pin11(_7489_1_pin11), .pin12(_7489_1_pin12), .pin13(_7489_1_pin13), .pin14(_7489_1_pin14),
    .pin15(_7489_1_pin15), .pin16(1'b1));
  _7404 NOT (
    .pin1(_7489_1_pin5), .pin2(NOT_pin2), .pin3(_7489_1_pin7), .pin4(NOT_pin4), .pin5(1'b0), .pin7(1'b0),
    .pin9(1'b0), .pin10(NOT_pin10), .pin11(_7489_1_pin9), .pin12(NOT_pin12), .pin13(_7489_1_pin11),
    .pin14(1'b1));  // open: pin6, pin8
  LED led_1 (.in(NOT_pin2));
  LED led_2 (.in(NOT_pin4));
  LED led_3 (.in(NOT_pin10));
  LED led_4 (.in(NOT_pin12));
  LED led_5 (.in(NOT_2_pin2));
  LED led_6 (.in(NOT_2_pin4));
  LED led_7 (.in(NOT_2_pin10));
  LED led_8 (.in(NOT_2_pin12));
  _74173 D_3_OUT (
    .pin1(1'b0), .pin2(1'b0), .pin3(D_3_OUT_pin3), .pin4(D_3_OUT_pin4), .pin5(D_3_OUT_pin5),
    .pin6(D_3_OUT_pin6), .pin7(CLK), .pin8(1'b0), .pin9(LOAD), .pin10(LOAD), .pin11(A4), .pin12(A3),
    .pin13(A2), .pin14(A1), .pin15(CLR), .pin16(1'b1));
  _7489 _7489_2 (
    .pin1(_7489_1_pin1), .pin2(1'b0), .pin3(WE), .pin4(_7489_2_pin4), .pin5(_7489_2_pin5),
    .pin6(_7489_2_pin6), .pin7(_7489_2_pin7), .pin8(1'b0), .pin9(_7489_2_pin9), .pin10(_7489_2_pin10),
    .pin11(_7489_2_pin11), .pin12(_7489_2_pin12), .pin13(_7489_1_pin13), .pin14(_7489_1_pin14),
    .pin15(_7489_1_pin15), .pin16(1'b1));
  _74173 D_3_OUT_2 (
    .pin1(1'b0), .pin2(1'b0), .pin3(D_3_OUT_2_pin3), .pin4(D_3_OUT_2_pin4), .pin5(D_3_OUT_2_pin5),
    .pin6(D_3_OUT_2_pin6), .pin7(CLK), .pin8(1'b0), .pin9(LOAD), .pin10(LOAD), .pin11(D4), .pin12(D3),
    .pin13(D2), .pin14(D1), .pin15(CLR_2), .pin16(1'b1));
  _74157 MUX (
    .pin1(SEL), .pin2(D_3_OUT_pin3), .pin3(MUX_pin3), .pin4(_7489_1_pin1), .pin5(D_3_OUT_pin4),
    .pin6(MUX_pin6), .pin7(_7489_1_pin15), .pin8(1'b0), .pin9(_7489_1_pin14), .pin10(MUX_pin10),
    .pin11(D_3_OUT_pin5), .pin12(_7489_1_pin13), .pin13(MUX_pin13), .pin14(D_3_OUT_pin6), .pin15(1'b0),
    .pin16(1'b1));
  _7404 NOT_2 (
    .pin1(_7489_2_pin5), .pin2(NOT_2_pin2), .pin3(_7489_2_pin7), .pin4(NOT_2_pin4), .pin5(1'b0), .pin7(1'b0),
    .pin9(1'b0), .pin10(NOT_2_pin10), .pin11(_7489_2_pin9), .pin12(NOT_2_pin12), .pin13(_7489_2_pin11),
    .pin14(1'b1));  // open: pin6, pin8
  _74157 MUX_2 (
    .pin1(SEL_2), .pin2(D_3_OUT_2_pin3), .pin3(MUX_2_pin3), .pin4(_7489_2_pin4), .pin5(D_3_OUT_2_pin4),
    .pin6(MUX_2_pin6), .pin7(_7489_2_pin6), .pin8(1'b0), .pin9(_7489_2_pin10), .pin10(MUX_2_pin10),
    .pin11(D_3_OUT_2_pin5), .pin12(_7489_2_pin12), .pin13(MUX_2_pin13), .pin14(D_3_OUT_2_pin6), .pin15(1'b0),
    .pin16(1'b1));
  _74126 _3_STATE (
    .pin1(EN), .pin2(NOT_2_pin2), .pin3(O1), .pin4(EN), .pin5(NOT_2_pin4), .pin6(O2), .pin7(1'b0), .pin8(O3),
    .pin9(NOT_2_pin10), .pin10(EN), .pin11(O4), .pin12(NOT_2_pin12), .pin13(EN), .pin14(1'b1));
  DipSwitch dipswitch_1 (.out(MUX_pin13));
  DipSwitch dipswitch_2 (.out(MUX_pin10));
  DipSwitch dipswitch_3 (.out(MUX_pin6));
  DipSwitch dipswitch_4 (.out(MUX_pin3));
  DipSwitch dipswitch_5 (.out(_7489_1_pin12));
  DipSwitch dipswitch_6 (.out(_7489_1_pin10));
  DipSwitch dipswitch_7 (.out(_7489_1_pin6));
  DipSwitch dipswitch_8 (.out(_7489_1_pin4));
  DipSwitch dipswitch_9 (.out(MUX_2_pin13));
  DipSwitch dipswitch_10 (.out(MUX_2_pin10));
  DipSwitch dipswitch_11 (.out(MUX_2_pin6));
  DipSwitch dipswitch_12 (.out(MUX_2_pin3));
  _7408 AND (
    .pin1(1'b1), .pin2(1'b1), .pin4(1'b0), .pin5(1'b0), .pin7(1'b0), .pin9(1'b1), .pin10(1'b1), .pin12(1'b1),
    .pin13(1'b1), .pin14(1'b1));  // open: pin3, pin6, pin8, pin11

  // Notes on the sheet:
  //   RAM Module
  //   MAR
  //   MDR
endmodule
