// Digital circuit RAM_Module_8-bit_V2_IC.dig as structural Verilog
module RAM_Module_8_bit_V2_IC (
  input  in_1,
  input  in_2,
  input  in_3,
  input  in_4,
  input  in_5,
  input  in_6,
  input  in_7,
  input  in_8,
  input  in_9,
  input  in_10,
  input  in_11,
  input  in_12,
  input  in_13,
  input  in_14
);

  wire _3_STATE_pin3, _3_STATE_pin6, _3_STATE_pin8, _3_STATE_pin11, _7489_1_pin5, _7489_1_pin7, _7489_1_pin9,
       _7489_1_pin11, _7489_2_pin5, _7489_2_pin7, _7489_2_pin9, _7489_2_pin11, NOT_2_pin2, NOT_2_pin4,
       NOT_2_pin8, NOT_2_pin10;

  _7489 _7489_1 (
    .pin1(in_2), .pin2(1'b0), .pin3(in_1), .pin4(in_6), .pin5(_7489_1_pin5), .pin6(in_7),
    .pin7(_7489_1_pin7), .pin8(1'b0), .pin9(_7489_1_pin9), .pin10(in_8), .pin11(_7489_1_pin11), .pin12(in_9),
    .pin13(in_5), .pin14(in_4), .pin15(in_3), .pin16(1'b1));
  _7489 _7489_2 (
    .pin1(in_2), .pin2(1'b0), .pin3(in_1), .pin4(in_10), .pin5(_7489_2_pin5), .pin6(in_11),
    .pin7(_7489_2_pin7), .pin8(1'b0), .pin9(_7489_2_pin9), .pin10(in_12), .pin11(_7489_2_pin11),
    .pin12(in_13), .pin13(in_5), .pin14(in_4), .pin15(in_3), .pin16(1'b1));
  _7404 NOT (
    .pin1(_7489_1_pin5), .pin3(_7489_1_pin7), .pin5(1'b0), .pin7(1'b0), .pin9(_7489_1_pin9),
    .pin11(_7489_1_pin11), .pin13(1'b0), .pin14(1'b1));  // open: pin2, pin4, pin6, pin8, pin10, pin12
  _7404 NOT_2 (
    .pin1(_7489_2_pin5), .pin2(NOT_2_pin2), .pin3(_7489_2_pin7), .pin4(NOT_2_pin4), .pin5(1'b0), .pin7(1'b0),
    .pin8(NOT_2_pin8), .pin9(_7489_2_pin9), .pin10(NOT_2_pin10), .pin11(_7489_2_pin11), .pin13(1'b0),
    .pin14(1'b1));  // open: pin6, pin12
  _74126 _3_STATE (
    .pin1(in_14), .pin2(NOT_2_pin2), .pin3(_3_STATE_pin3), .pin4(in_14), .pin5(NOT_2_pin4),
    .pin6(_3_STATE_pin6), .pin7(1'b0), .pin8(_3_STATE_pin8), .pin9(NOT_2_pin8), .pin10(in_14),
    .pin11(_3_STATE_pin11), .pin12(NOT_2_pin10), .pin13(in_14), .pin14(1'b1));
endmodule
