// Digital circuit Reg_IC.dig as structural Verilog
module Reg_IC (
  input  D1,
  input  D2,
  input  D3,
  input  D4,
  input  EO,
  input  CLK,
  input  CLR,
  input  LOAD,
  output O1,
  output O2,
  output O3,
  output O4
);

  wire D_3_OUT_pin3, D_3_OUT_pin4, D_3_OUT_pin5, D_3_OUT_pin6;

  _74173 D_3_OUT (
    .pin1(1'b0), .pin2(1'b0), .pin3(D_3_OUT_pin3), .pin4(D_3_OUT_pin4), .pin5(D_3_OUT_pin5),
    .pin6(D_3_OUT_pin6), .pin7(CLK), .pin8(1'b0), .pin9(LOAD), .pin10(LOAD), .pin11(D4), .pin12(D3),
    .pin13(D2), .pin14(D1), .pin15(CLR), .pin16(1'b1));
  _74126 _3_STATE (
    .pin1(EO), .pin2(D_3_OUT_pin3), .pin3(O1), .pin4(EO), .pin5(D_3_OUT_pin4), .pin6(O2), .pin7(1'b0),
    .pin8(O3), .pin9(D_3_OUT_pin5), .pin10(EO), .pin11(O4), .pin12(D_3_OUT_pin6), .pin13(EO), .pin14(1'b1));
endmodule
