// Digital circuit RAM_using_DIL.dig as structural Verilog
module RAM_using_DIL (
  input  _3,
  input  _2,
  input  _1,
  input  _0,
  input  OUT,
  input  WE,
  input  SEL,
  input  LD,
  input  D3,
  input  D2,
  input  D1,
  input  D0,
  input  CLK,
  output O3,
  output O2,
  output O1,
  output O0
);

  wire _74189_1_pin2, _74189_1_pin5, _74189_1_pin7, _74189_1_pin9, _74189_1_pin11, and_1_out, and_2_out,
       and_3_out, and_4_out, and_5_out, and_6_out, and_7_out, and_8_out, and_9_out, and_10_out, and_11_out,
       and_12_out, and_13_out, and_14_out, and_15_out, and_16_out, and_17_out, d_latch_1_q, d_latch_2_q,
       d_latch_3_q, d_latch_4_q, dipswitch_1_out, dipswitch_2_out, dipswitch_3_out, dipswitch_4_out,
       not_1_out, not_2_out, not_3_out, not_4_out, not_5_out, not_6_out, not_8_out, not_9_out, not_10_out,
       not_11_out, or_1_out, or_2_out, or_3_out, or_4_out, or_5_out, or_6_out, or_7_out, or_8_out;

  LED led_1 (.in(not_5_out));
  not not_1 (not_1_out, LD);
  not not_2 (not_2_out, LD);
  not not_3 (not_3_out, LD);
  not not_4 (not_4_out, LD);
  and and_1 (and_1_out, d_latch_1_q, not_1_out);
  and and_2 (and_2_out, LD, D3);
  and and_3 (and_3_out, d_latch_2_q, not_2_out);
  and and_4 (and_4_out, LD, D2);
  and and_5 (and_5_out, d_latch_3_q, not_3_out);
  and and_6 (and_6_out, LD, D1);
  and and_7 (and_7_out, d_latch_4_q, not_4_out);
  and and_8 (and_8_out, LD, D0);
  not not_5 (not_5_out, SEL);
  or or_1 (or_1_out, and_1_out, and_2_out);
  or or_2 (or_2_out, and_3_out, and_4_out);
  or or_3 (or_3_out, and_5_out, and_6_out);
  or or_4 (or_4_out, and_7_out, and_8_out);
  D_Latch d_latch_1 (.IN(or_1_out), .EN(CLK), .Q(d_latch_1_q));  // open: Q_2
  D_Latch d_latch_2 (.IN(or_2_out), .EN(CLK), .Q(d_latch_2_q));  // open: Q_2
  D_Latch d_latch_3 (.IN(or_3_out), .EN(CLK), .Q(d_latch_3_q));  // open: Q_2
  D_Latch d_latch_4 (.IN(or_4_out), .EN(CLK), .Q(d_latch_4_q));  // open: Q_2
  LED led_2 (.in(SEL));
  DipSwitch dipswitch_1 (.out(dipswitch_1_out));
  DipSwitch dipswitch_2 (.out(dipswitch_2_out));
  DipSwitch dipswitch_3 (.out(dipswitch_3_out));
  DipSwitch dipswitch_4 (.out(dipswitch_4_out));
  and and_9 (and_9_out, not_5_out, d_latch_1_q);
  and and_10 (and_10_out, SEL, dipswitch_1_out);
  and and_11 (and_11_out, not_5_out, d_latch_2_q);
  and and_12 (and_12_out, SEL, dipswitch_2_out);
  and and_13 (and_13_out, not_5_out, d_latch_3_q);
  and and_14 (and_14_out, SEL, dipswitch_3_out);
  and and_15 (and_15_out, not_5_out, d_latch_4_q);
  and and_16 (and_16_out, SEL, dipswitch_4_out);
  or or_5 (or_5_out, and_9_out, and_10_out);
  or or_6 (or_6_out, and_11_out, and_12_out);
  or or_7 (or_7_out, and_13_out, and_14_out);
  or or_8 (or_8_out, and_15_out, and_16_out);
  and and_17 (and_17_out, OUT, CLK);
  not not_6 (not_6_out, WE);
  _74189 _74189_1 (
    .pin1(or_8_out), .pin2(_74189_1_pin2), .pin3(not_6_out), .pin4(_0), .pin5(_74189_1_pin5), .pin6(_1),
    .pin7(_74189_1_pin7), .pin8(1'b0), .pin9(_74189_1_pin9), .pin10(_2), .pin11(_74189_1_pin11), .pin12(_3),
    .pin13(or_5_out), .pin14(or_6_out), .pin15(or_7_out), .pin16(1'b1));
  not not_7 (_74189_1_pin2, 1'b1);
  not not_8 (not_8_out, _74189_1_pin11);
  not not_9 (not_9_out, _74189_1_pin9);
  not not_10 (not_10_out, _74189_1_pin7);
  not not_11 (not_11_out, _74189_1_pin5);
  Tri_State_Buffer tri_state_buffer_1 (.IN(not_8_out), .EN(and_17_out), .OUT(O3));
  Tri_State_Buffer tri_state_buffer_2 (.IN(not_10_out), .EN(and_17_out), .OUT(O1));
  Tri_State_Buffer tri_state_buffer_3 (.IN(not_9_out), .EN(and_17_out), .OUT(O2));
  Tri_State_Buffer tri_state_buffer_4 (.IN(not_11_out), .EN(and_17_out), .OUT(O0));

  // Notes on the sheet:
  //   Data IN
  //   Select Loc
endmodule
