// Digital circuit Program_Counter_IC.dig as structural Verilog
module Program_Counter_IC (
  input  A1,
  input  A2,
  input  A3,
  input  A4,
  input  EN,
  input  LOAD,
  input  EO,
  input  CLK,
  input  CLR,
  output _1,
  output _2,
  output _3,
  output _4
);

  wire _74163_1_pin11, _74163_1_pin12, _74163_1_pin13, _74163_1_pin14;

  _74163 _74163_1 (
    .pin1(CLR), .pin2(CLK), .pin3(A1), .pin4(A2), .pin5(A3), .pin6(A4), .pin7(EN), .pin8(1'b0), .pin9(LOAD),
    .pin10(EN), .pin11(_74163_1_pin11), .pin12(_74163_1_pin12), .pin13(_74163_1_pin13),
    .pin14(_74163_1_pin14), .pin16(1'b1));  // open: pin15
  _74126 _3_STATE (
    .pin1(EO), .pin2(_74163_1_pin14), .pin3(_1), .pin4(EO), .pin5(_74163_1_pin13), .pin6(_2), .pin7(1'b0),
    .pin8(_3), .pin9(_74163_1_pin12), .pin10(EO), .pin11(_4), .pin12(_74163_1_pin11), .pin13(EO), .pin14(1'b1));
endmodule
