// Digital circuit RAM_using_74LS189.dig as structural Verilog
module RAM_using_74LS189 (
  input  D0,
  input  D1,
  input  D2,
  input  D3,
  input  OUT,
  input  CLK,
  input  A0,
  input  A1,
  input  A2,
  input  A3,
  output O0,
  output O1,
  output O2,
  output O3
);

  wire _74189_1_pin5, _74189_1_pin7, _74189_1_pin9, _74189_1_pin11, and_1_out, not_1_out, not_2_out,
       not_3_out, not_4_out;

  and and_1 (and_1_out, CLK, OUT);
  _74189 _74189_1 (
    .pin1(A0), .pin4(D0), .pin5(_74189_1_pin5), .pin6(D1), .pin7(_74189_1_pin7), .pin8(1'b0),
    .pin9(_74189_1_pin9), .pin10(D2), .pin11(_74189_1_pin11), .pin12(D3), .pin13(A3), .pin14(A2), .pin15(A1),
    .pin16(1'b1));  // open: pin2, pin3
  not not_1 (not_1_out, _74189_1_pin5);
  not not_2 (not_2_out, _74189_1_pin7);
  not not_3 (not_3_out, _74189_1_pin9);
  not not_4 (not_4_out, _74189_1_pin11);
  Tri_State_Buffer tri_state_buffer_1 (.IN(not_1_out), .EN(and_1_out), .OUT(O0));
  Tri_State_Buffer tri_state_buffer_2 (.IN(not_3_out), .EN(and_1_out), .OUT(O2));
  Tri_State_Buffer tri_state_buffer_3 (.IN(not_2_out), .EN(and_1_out), .OUT(O1));
  Tri_State_Buffer tri_state_buffer_4 (.IN(not_4_out), .EN(and_1_out), .OUT(O3));
endmodule
