// Digital circuit Tri-State_Buffer.dig as structural Verilog
module Tri_State_Buffer (
  input  IN,
  input  EN,
  output OUT
);

  wire nand_1_out, nor_1_out, not_1_out;

  not not_1 (not_1_out, EN);
  nand nand_1 (nand_1_out, IN, EN);
  nor nor_1 (nor_1_out, IN, not_1_out);
  PFET pfet_1 (.G(nand_1_out), .S(1'b1), .D(OUT));
  NFET nfet_1 (.G(nor_1_out), .D(OUT), .S(1'b0));
endmodule
